# Fritzing sketch MoistureSensor (saved by Fritzing 0.9.4)

parts:
  Part1 = Soil Moisture Sensor
  VCC1 = Battery
  U1 = SIP - 6 pins [chip_label=IC package="SIP (Single Inline) [THT]"]

nets:
  N1: Part1.SIG, U1.IO2
  GND: Part1.GND, VCC1.-, U1.GND
  VCC: Part1.VCC, U1.3V3
  N2: VCC1.+, U1.BATT

custom parts:
  SIP - 6 pins: A SIP stand-in part for whatever you want. With 6 pins on a 300 mil single inline package (SIP) footprint.
